# Fritzing sketch ArduinoOpticalTransmit-Receive (saved by Fritzing 0.9.3b)

parts:
  Part1 = Arduino Uno (Rev3) - ICSP
  R1 = Resistor [tolerance=±5% resistance=510 package="2010 [SMD]"]
  U2 = 7-SEGMENT-4DIGIT [package=7-segment-4digit-youngsun]  # not connected
  U3 = 7-SEGMENT-4DIGIT [package=7-segment-4digit-youngsun]  # not connected
  Q1 = LTR-301 [package=ltr-301]
  U4 = mystery part, 4 pins [chip_label=BMP280]
  U5 = mystery part, 3 pins [chip_label=KY-008]
  Part2 = Arduino Uno (Rev3) - ICSP
  Part4 = RobotDyn UNO R3 CH340
  Part3 = RobotDyn UNO R3 CH340  # not connected
  R2 = Resistor [tolerance=±5% resistance=220 package=THT]
  R3 = Resistor [tolerance=±5% resistance=220 package=THT]
  R4 = Resistor [tolerance=±5% resistance=220 package=THT]
  LED1 = LED - 3mm [color="Red (633nm)" package="3 mm [THT]"]
  LED2 = LED - 3mm [color="Green (565nm)" package="3 mm [THT]"]
  LED3 = LED - 3mm [color="Yellow (595nm)" package="3 mm [THT]"]

nets:
  N1: Part1.D5_PWM, R4.Pin_0
  N2: Part1.D6_PWM, R3.Pin_0
  N3: Part1.D7, R2.Pin_0
  N4: Part1.5V, R1.Pin_0
  N5: Part1.GND, Q1.C
  N6: R1.Pin_1, Q1.E, Part4.D9_PWM
  N7: U4.pin1, Part2.5V
  N8: U4.pin2, U5.pin3, Part2.GND
  N9: U4.pin3, Part2.A5/SCL
  N10: U4.pin4, Part2.A4/SDA
  N11: U5.pin1, Part2.D13/SCK
  N12: R2.Pin_1, LED3.anode
  N13: R3.Pin_1, LED2.anode
  N14: R4.Pin_1, LED1.anode

notes:
  LOAD
  CLK
  DIN
  Vcc
  GND
  Laser Receiver Phototransistor
  7 Segment Display
  5mW 650nm Red Laser Transmitter
  _
  S
  Temp/Pressure/Humidity Sensor
  (Detector portion of QRD1114)
  SDA
  SCL
  VIN
  Emitter
  Collector
  510 Ohm
  Generic LEDs

custom parts:
  RobotDyn UNO R3 CH340: Uno R3 CH340G/ATmega328P - compatible with the Arduino Uno R3 board, based on the microcontroller ATmega328P (SMD-version) and USB-UART interface chip CH340G.
